// Logisim project cpu.circ as structural Verilog: 10 circuits, main circuit main
module main (
  input  reset
);

  wire alu_3_overflow, ALUinB, and_1_out, and_2_out, beqBoolean, BLT, bltBoolean, BR, clk, DMwe, inputTrue,
       JAL, JP, JR, keyboard_1_avail, memory_latch_1_oe_latched, memory_latch_1_we_latched, notClock,
       or_1_out, outputTrue, Rdst, Rwd, Rwe, Rwsll, RwSRL;
  wire [1:0] ALUop;
  wire [2:0] multiplexer_2_out, multiplexer_3_out;
  wire [6:0] keyboard_1_data;
  wire [7:0] keyboardOut;
  wire [11:0] address;
  wire [15:0] alu_2_r, alu_3_r, ext_imm, leftshifter_1_slloutput, memory_latch_1_address_latched,
       memory_latch_1_data_in_latched, multiplexer_4_out, multiplexer_5_out, multiplexer_6_out,
       multiplexer_7_out, multiplexer_8_out, multiplexer_9_out, multiplexer_10_out, multiplexer_11_out,
       multiplexer_12_out, multiplexer_13_out, o0, o1, o2, o3, o4, o5, o6, o7, one_register_1_q, PCplusOne,
       ram_1_dout, registerfile_1_rs2val, rightshifter_1_srloutput, RS1;
  wire [15:12] rom_1_data;

  Keyboard keyboard_1 (.clk(notClock), .re(inputTrue), .clr(reset), .avail(keyboard_1_avail), .data(keyboard_1_data));
  TTY #(.rows(13), .cols(80)) tty_1 (.data(RS1[6:0]), .clk(clk), .we(outputTrue), .clr(reset));
  Clock clock_1 (.out(clk));
  not not_1 (notClock, clk);
  not not_2 (keyboardOut[7], keyboard_1_avail);
  one_register one_register_1 (.D(multiplexer_6_out), .WE(1'b1), .clk(notClock), .rst(reset), .Q(one_register_1_q));
  // Probe on one_register_1_q
  Multiplexer #(.width(7), .enable("false")) multiplexer_1 (
    .in0(keyboard_1_data), .in1({7{1'b0}}), .out(keyboardOut[6:0]), .sel(keyboardOut[7]));
  ROM #(.addrWidth(16), .dataWidth(16)) rom_1 (.addr(one_register_1_q), .data({rom_1_data, address}));
  ALU alu_1 (.R(PCplusOne), .A(one_register_1_q), .B(16'h1), .operation(2'b00));  // open: z, overflow
  // Probe on ext_imm
  Multiplexer #(.width(3), .enable("false")) multiplexer_2 (
    .in0(address[8:6]), .in1(address[5:3]), .out(multiplexer_2_out), .sel(Rdst));
  ALU alu_2 (.R(alu_2_r), .A(PCplusOne), .B(ext_imm), .operation(2'b00));  // open: z, overflow
  and and_1 (and_1_out, BR, beqBoolean);
  or or_1 (or_1_out, and_1_out, and_2_out);
  and and_2 (and_2_out, BLT, bltBoolean);
  Multiplexer #(.width(3), .enable("false")) multiplexer_3 (
    .in0(multiplexer_2_out), .in1(3'b111), .out(multiplexer_3_out), .sel(JAL));
  // Probe on {rom_1_data, address}
  // Probe on address
  // Probe on address[11:9]
  // Probe on address[8:6]
  // Probe on address[5:0]
  Multiplexer #(.width(16), .enable("false")) multiplexer_4 (
    .in0(PCplusOne), .in1(alu_2_r), .out(multiplexer_4_out), .sel(or_1_out));
  Multiplexer #(.width(16), .enable("false")) multiplexer_5 (
    .in0(multiplexer_4_out), .in1({4'b0000, address}), .out(multiplexer_5_out), .sel(JP));
  // Probe on address[5:3]
  // Probe on address[2:0]
  Multiplexer #(.width(16), .enable("false")) multiplexer_6 (
    .in0(multiplexer_7_out), .in1({4'b0000, address}), .out(multiplexer_6_out), .sel(JAL));
  // Probe on multiplexer_8_out
  Multiplexer #(.width(16), .enable("false")) multiplexer_7 (
    .in0(multiplexer_5_out), .in1(multiplexer_8_out), .out(multiplexer_7_out), .sel(JR));
  Multiplexer #(.width(16), .enable("false")) multiplexer_8 (
    .in0(multiplexer_11_out), .in1({{8{1'b0}}, keyboardOut}), .out(multiplexer_8_out), .sel(inputTrue));
  RegisterFile registerfile_1 (
    .rdval(multiplexer_8_out), .clk(clk), .reset(reset), .RegWriteEnable(Rwe), .writeReg(multiplexer_3_out),
    .ReadReg1(address[11:9]), .ReadReg2(address[8:6]), .rs1val(RS1), .rs2val(registerfile_1_rs2val), .o0(o0),
    .o1(o1), .o2(o2), .o3(o3), .o4(o4), .o5(o5), .o6(o6), .o7(o7));
  control control_1 (
    .opcode(rom_1_data), .BR(BR), .JP(JP), .Rdst(Rdst), .DMwe(DMwe), .ALUop(ALUop), .ALUinB(ALUinB),
    .Rwd(Rwd), .Rwe(Rwe), .RwSSL(Rwsll), .RwSRL(RwSRL), .BLT(BLT), .JR(JR), .JAL(JAL), .inputTrue(inputTrue),
    .outputTrue(outputTrue));
  assign ext_imm = {{10{address[5]}}, address[5:0]};  // Bit_Extender bit_extender_1
  // Probe on RS1
  Multiplexer #(.width(16), .enable("false")) multiplexer_9 (
    .in0(registerfile_1_rs2val), .in1(ext_imm), .out(multiplexer_9_out), .sel(ALUinB));
  ALU alu_3 (.R(alu_3_r), .A(RS1), .B(multiplexer_9_out), .z(beqBoolean), .operation(ALUop), .overflow(alu_3_overflow));
  // Probe on ALUop
  // Probe on o0
  // Probe on o1
  // Probe on o2
  // Probe on o3
  // Probe on o4
  // Probe on o5
  // Probe on o6
  // Probe on o6
  // Probe on o7
  // Probe on o7
  xor xor_1 (bltBoolean, alu_3_overflow, alu_3_r[15]);
  RAM #(.addrWidth(16), .dataWidth(16), .trigger("high"), .databus("bibus")) ram_1 (
    .addr(memory_latch_1_address_latched), .we(memory_latch_1_we_latched), .oe(memory_latch_1_oe_latched),
    .din(memory_latch_1_data_in_latched), .dout(ram_1_dout));
  memory_latch memory_latch_1 (
    .address(alu_3_r), .WE(DMwe), .clk(notClock), .data_in(registerfile_1_rs2val),
    .address_latched(memory_latch_1_address_latched), .WE_latched(memory_latch_1_we_latched),
    .OE_latched(memory_latch_1_oe_latched), .data_in_latched(memory_latch_1_data_in_latched));
  Multiplexer #(.width(16), .enable("false")) multiplexer_10 (
    .in0(alu_3_r), .in1(ram_1_dout), .out(multiplexer_10_out), .sel(Rwd));
  // Probe on ram_1_dout
  Multiplexer #(.width(16), .enable("false")) multiplexer_11 (
    .in0(multiplexer_13_out), .in1(PCplusOne), .out(multiplexer_11_out), .sel(JAL));
  Multiplexer #(.width(16), .enable("false")) multiplexer_12 (
    .in0(multiplexer_10_out), .in1(leftshifter_1_slloutput), .out(multiplexer_12_out), .sel(Rwsll));
  leftShifter leftshifter_1 (
    .shiftInput(multiplexer_10_out), .shiftAmount(address[2:0]), .sllOutput(leftshifter_1_slloutput));
  Multiplexer #(.width(16), .enable("false")) multiplexer_13 (
    .in0(multiplexer_12_out), .in1(rightshifter_1_srloutput), .out(multiplexer_13_out), .sel(RwSRL));
  rightShifter rightshifter_1 (
    .shiftInput(multiplexer_12_out), .shiftAmount(address[2:0]), .srlOutput(rightshifter_1_srloutput));

  // Other names for the same wires on the sheet: imm[5:0] = address[5:0]; shamt[2:0] = address[2:0];
  //   rd[2:0] = address[5:3]; rt[2:0] = address[8:6]; rs[2:0] = address[11:9]

  // Notes on the sheet:
  //   Note: this is just to debug registers. It can be removed
endmodule

module one_register (
  input  [15:0] D,
  input  WE,
  input  clk,
  input  rst,
  output [15:0] Q
);

  wire clk_t;

  D_Flip_Flop d_ff_1 (.D(D[0]), .clk(clk_t), .Q(Q[0]), .reset(rst));  // open: Qn, preset
  D_Flip_Flop d_ff_2 (.D(D[1]), .clk(clk_t), .Q(Q[1]), .reset(rst));  // open: Qn, preset
  D_Flip_Flop d_ff_3 (.D(D[2]), .clk(clk_t), .Q(Q[2]), .reset(rst));  // open: Qn, preset
  D_Flip_Flop d_ff_4 (.D(D[3]), .clk(clk_t), .Q(Q[3]), .reset(rst));  // open: Qn, preset
  and and_1 (clk_t, WE, clk);
  D_Flip_Flop d_ff_5 (.D(D[8]), .clk(clk_t), .Q(Q[8]), .reset(rst));  // open: Qn, preset
  D_Flip_Flop d_ff_6 (.D(D[9]), .clk(clk_t), .Q(Q[9]), .reset(rst));  // open: Qn, preset
  D_Flip_Flop d_ff_7 (.D(D[10]), .clk(clk_t), .Q(Q[10]), .reset(rst));  // open: Qn, preset
  D_Flip_Flop d_ff_8 (.D(D[11]), .clk(clk_t), .Q(Q[11]), .reset(rst));  // open: Qn, preset
  D_Flip_Flop d_ff_9 (.D(D[4]), .clk(clk_t), .Q(Q[4]), .reset(rst));  // open: Qn, preset
  D_Flip_Flop d_ff_10 (.D(D[5]), .clk(clk_t), .Q(Q[5]), .reset(rst));  // open: Qn, preset
  D_Flip_Flop d_ff_11 (.D(D[6]), .clk(clk_t), .Q(Q[6]), .reset(rst));  // open: Qn, preset
  D_Flip_Flop d_ff_12 (.D(D[7]), .clk(clk_t), .Q(Q[7]), .reset(rst));  // open: Qn, preset
  D_Flip_Flop d_ff_13 (.D(D[12]), .clk(clk_t), .Q(Q[12]), .reset(rst));  // open: Qn, preset
  D_Flip_Flop d_ff_14 (.D(D[13]), .clk(clk_t), .Q(Q[13]), .reset(rst));  // open: Qn, preset
  D_Flip_Flop d_ff_15 (.D(D[14]), .clk(clk_t), .Q(Q[14]), .reset(rst));  // open: Qn, preset
  D_Flip_Flop d_ff_16 (.D(D[15]), .clk(clk_t), .Q(Q[15]), .reset(rst));  // open: Qn, preset

  // Other names for the same wires on the sheet: in0 = D[0]; in1 = D[1]; in2 = D[2]; in3 = D[3]; in4 = D[4];
  //   in5 = D[5]; in6 = D[6]; in7 = D[7]; in8 = D[8]; in9 = D[9]; in10 = D[10]; in11 = D[11]; in12 = D[12];
  //   in13 = D[13]; in14 = D[14]; in15 = D[15]; out0 = Q[0]; out1 = Q[1]; out2 = Q[2]; out3 = Q[3]; out4 = Q[4];
  //   out5 = Q[5]; out6 = Q[6]; out7 = Q[7]; out8 = Q[8]; out9 = Q[9]; out10 = Q[10]; out11 = Q[11]; out12 = Q[12];
  //   out13 = Q[13]; out14 = Q[14]; out15 = Q[15]
endmodule

module ALU (
  input  [15:0] A,
  input  [15:0] B,
  input  [1:0] operation,
  output z,
  output [15:0] R,
  output overflow
);

  wire or_1_out, sixteenbitadder_1_overflow, sixteenbitadder_2_overflow;
  wire [15:0] not_1_out, sixteenbitadder_1_result, sixteenbitadder_2_result, xor_1_out;

  assign xor_1_out = A ^ B;  // XOR_Gate xor_1, 16 bits wide
  assign not_1_out = ~A;  // NOT_Gate not_1, 16 bits wide
  sixteenbitadder sixteenbitadder_1 (
    .sub(1'b0), .A(A), .B(B), .result(sixteenbitadder_1_result), .overflow(sixteenbitadder_1_overflow));
  sixteenbitadder sixteenbitadder_2 (
    .sub(1'b1), .A(A), .B(B), .result(sixteenbitadder_2_result), .overflow(sixteenbitadder_2_overflow));
  Multiplexer #(.select(2), .width(16), .enable("false")) multiplexer_1 (
    .in0(sixteenbitadder_1_result), .in1(sixteenbitadder_2_result), .in2(xor_1_out), .in3(not_1_out),
    .out(R), .sel(operation));
  Multiplexer #(.select(2), .enable("false")) multiplexer_2 (
    .in0(sixteenbitadder_1_overflow), .in1(sixteenbitadder_2_overflow), .in2(1'b0), .in3(1'b0),
    .out(overflow), .sel(operation));
  or or_1 (or_1_out, R[0], R[1], R[2], R[3], R[4], R[5], R[6], R[7], R[8], R[9], R[10], R[11], R[12], R[13], R[14], R[15]);
  not not_2 (z, or_1_out);
endmodule

module RegisterFile (
  input  [15:0] rdval,
  input  clk,
  input  reset,
  input  RegWriteEnable,
  input  [2:0] writeReg,
  input  [2:0] ReadReg1,
  input  [2:0] ReadReg2,
  output [15:0] rs1val,
  output [15:0] rs2val,
  output [15:0] o0,
  output [15:0] o1,
  output [15:0] o2,
  output [15:0] o3,
  output [15:0] o4,
  output [15:0] o5,
  output [15:0] o6,
  output [15:0] o7
);

  wire r10, r11, r12, r13, r14, r15, r16, r17, r20, r21, r22, r23, r24, r25, r26, r27, write0, write1,
       write2, write3, write4, write5, write6, write7;

  Decoder #(.select(3)) decoder_1 (
    .out0(write0), .out1(write1), .out2(write2), .out3(write3), .out4(write4), .out5(write5), .out6(write6),
    .out7(write7), .sel(writeReg), .en(RegWriteEnable));
  Decoder #(.select(3), .enable("false")) decoder_2 (
    .out0(r10), .out1(r11), .out2(r12), .out3(r13), .out4(r14), .out5(r15), .out6(r16), .out7(r17),
    .sel(ReadReg1));
  Decoder #(.select(3), .enable("false")) decoder_3 (
    .out0(r20), .out1(r21), .out2(r22), .out3(r23), .out4(r24), .out5(r25), .out6(r26), .out7(r27),
    .sel(ReadReg2));
  assign rs1val = r10 ? {16{1'b0}} : 16'bz;  // Controlled_Buffer controlled_buffer_1
  assign rs1val = r11 ? o1 : 16'bz;  // Controlled_Buffer controlled_buffer_2
  assign rs1val = r12 ? o2 : 16'bz;  // Controlled_Buffer controlled_buffer_3
  assign rs1val = r13 ? o3 : 16'bz;  // Controlled_Buffer controlled_buffer_4
  assign rs1val = r14 ? o4 : 16'bz;  // Controlled_Buffer controlled_buffer_5
  assign rs1val = r15 ? o5 : 16'bz;  // Controlled_Buffer controlled_buffer_6
  assign rs1val = r16 ? o6 : 16'bz;  // Controlled_Buffer controlled_buffer_7
  assign rs1val = r17 ? o7 : 16'bz;  // Controlled_Buffer controlled_buffer_8
  assign rs2val = r20 ? {16{1'b0}} : 16'bz;  // Controlled_Buffer controlled_buffer_9
  assign rs2val = r21 ? o1 : 16'bz;  // Controlled_Buffer controlled_buffer_10
  assign rs2val = r22 ? o2 : 16'bz;  // Controlled_Buffer controlled_buffer_11
  assign rs2val = r23 ? o3 : 16'bz;  // Controlled_Buffer controlled_buffer_12
  assign rs2val = r24 ? o4 : 16'bz;  // Controlled_Buffer controlled_buffer_13
  assign rs2val = r25 ? o5 : 16'bz;  // Controlled_Buffer controlled_buffer_14
  assign rs2val = r26 ? o6 : 16'bz;  // Controlled_Buffer controlled_buffer_15
  assign rs2val = r27 ? o7 : 16'bz;  // Controlled_Buffer controlled_buffer_16
  // Probe on {16{1'b0}}
  one_register one_register_1 (.D(rdval), .WE(write1), .clk(clk), .rst(reset), .Q(o1));
  one_register one_register_2 (.D(rdval), .WE(write2), .clk(clk), .rst(reset), .Q(o2));
  one_register one_register_3 (.D(rdval), .WE(write3), .clk(clk), .rst(reset), .Q(o3));
  one_register one_register_4 (.D(rdval), .WE(write4), .clk(clk), .rst(reset), .Q(o4));
  one_register one_register_5 (.D(rdval), .WE(write5), .clk(clk), .rst(reset), .Q(o5));
  one_register one_register_6 (.D(rdval), .WE(write6), .clk(clk), .rst(reset), .Q(o6));
  one_register one_register_7 (.D(rdval), .WE(write7), .clk(clk), .rst(reset), .Q(o7));
  // Probe on o1
  // Probe on o2
  // Probe on o3
  // Probe on o4
  // Probe on o5
  // Probe on o6
  // Probe on o7

  assign o0 = {16{1'b0}};

  // Other names for the same wires on the sheet: out1[15:0] = o1; out2[15:0] = o2; out3[15:0] = o3; out4[15:0] = o4;
  //   out5[15:0] = o5; out6[15:0] = o6; out7[15:0] = o7; rst = reset
endmodule

module sixteenbitadder (
  input  sub,
  input  [15:0] A,
  input  [15:0] B,
  output [15:0] result,
  output overflow
);

  wire onebitadder_1_cout, onebitadder_2_cout, onebitadder_3_cout, onebitadder_4_cout, onebitadder_5_cout,
       onebitadder_6_cout, onebitadder_7_cout, onebitadder_8_cout, onebitadder_9_cout, onebitadder_10_cout,
       onebitadder_11_cout, onebitadder_12_cout, onebitadder_13_cout, onebitadder_14_cout,
       onebitadder_15_cout, onebitadder_16_cout, xor_1_out, xor_2_out, xor_3_out, xor_4_out, xor_5_out,
       xor_6_out, xor_7_out, xor_8_out, xor_9_out, xor_10_out, xor_11_out, xor_12_out, xor_13_out,
       xor_14_out, xor_15_out, xor_16_out;

  xor xor_1 (xor_1_out, sub, B[0]);
  xor xor_2 (xor_2_out, sub, B[1]);
  xor xor_3 (xor_3_out, sub, B[2]);
  xor xor_4 (xor_4_out, sub, B[3]);
  xor xor_5 (xor_5_out, sub, B[4]);
  xor xor_6 (xor_6_out, sub, B[5]);
  xor xor_7 (xor_7_out, sub, B[6]);
  xor xor_8 (xor_8_out, sub, B[7]);
  xor xor_9 (xor_9_out, sub, B[8]);
  xor xor_10 (xor_10_out, sub, B[9]);
  xor xor_11 (xor_11_out, sub, B[10]);
  xor xor_12 (xor_12_out, sub, B[11]);
  xor xor_13 (xor_13_out, sub, B[12]);
  xor xor_14 (xor_14_out, sub, B[13]);
  xor xor_15 (xor_15_out, sub, B[14]);
  xor xor_16 (xor_16_out, sub, B[15]);
  onebitadder onebitadder_1 (.cin(sub), .a(xor_1_out), .b(A[0]), .sum(result[0]), .cout(onebitadder_1_cout));
  onebitadder onebitadder_2 (
    .cin(onebitadder_1_cout), .a(xor_2_out), .b(A[1]), .sum(result[1]), .cout(onebitadder_2_cout));
  onebitadder onebitadder_3 (
    .cin(onebitadder_2_cout), .a(xor_3_out), .b(A[2]), .sum(result[2]), .cout(onebitadder_3_cout));
  onebitadder onebitadder_4 (
    .cin(onebitadder_3_cout), .a(xor_4_out), .b(A[3]), .sum(result[3]), .cout(onebitadder_4_cout));
  onebitadder onebitadder_5 (
    .cin(onebitadder_4_cout), .a(xor_5_out), .b(A[4]), .sum(result[4]), .cout(onebitadder_5_cout));
  onebitadder onebitadder_6 (
    .cin(onebitadder_5_cout), .a(xor_6_out), .b(A[5]), .sum(result[5]), .cout(onebitadder_6_cout));
  onebitadder onebitadder_7 (
    .cin(onebitadder_6_cout), .a(xor_7_out), .b(A[6]), .sum(result[6]), .cout(onebitadder_7_cout));
  onebitadder onebitadder_8 (
    .cin(onebitadder_7_cout), .a(xor_8_out), .b(A[7]), .sum(result[7]), .cout(onebitadder_8_cout));
  onebitadder onebitadder_9 (
    .cin(onebitadder_8_cout), .a(xor_9_out), .b(A[8]), .sum(result[8]), .cout(onebitadder_9_cout));
  onebitadder onebitadder_10 (
    .cin(onebitadder_9_cout), .a(xor_10_out), .b(A[9]), .sum(result[9]), .cout(onebitadder_10_cout));
  onebitadder onebitadder_11 (
    .cin(onebitadder_10_cout), .a(xor_11_out), .b(A[10]), .sum(result[10]), .cout(onebitadder_11_cout));
  onebitadder onebitadder_12 (
    .cin(onebitadder_11_cout), .a(xor_12_out), .b(A[11]), .sum(result[11]), .cout(onebitadder_12_cout));
  onebitadder onebitadder_13 (
    .cin(onebitadder_12_cout), .a(xor_13_out), .b(A[12]), .sum(result[12]), .cout(onebitadder_13_cout));
  onebitadder onebitadder_14 (
    .cin(onebitadder_13_cout), .a(xor_14_out), .b(A[13]), .sum(result[13]), .cout(onebitadder_14_cout));
  onebitadder onebitadder_15 (
    .cin(onebitadder_14_cout), .a(xor_15_out), .b(A[14]), .sum(result[14]), .cout(onebitadder_15_cout));
  onebitadder onebitadder_16 (
    .cin(onebitadder_15_cout), .a(xor_16_out), .b(A[15]), .sum(result[15]), .cout(onebitadder_16_cout));
  xor xor_17 (overflow, onebitadder_15_cout, onebitadder_16_cout);
endmodule

module onebitadder (
  input  cin,
  input  a,
  input  b,
  output sum,
  output cout
);

  wire and_1_out, and_2_out, xor_1_out;

  xor xor_1 (xor_1_out, a, b);
  and and_1 (and_1_out, a, b);
  and and_2 (and_2_out, cin, xor_1_out);
  xor xor_2 (sum, cin, xor_1_out);
  or or_1 (cout, and_2_out, and_1_out);
endmodule

module memory_latch (
  input  [15:0] address,
  input  WE,
  input  clk,
  input  [15:0] data_in,
  output [15:0] address_latched,
  output WE_latched,
  output OE_latched,
  output [15:0] data_in_latched
);

  wire DMwe_latch_q;
  wire [15:0] addr_latch_q;

  Register #(.width(16), .trigger("falling")) addr_latch (
    .D(address), .en(WE), .clk(clk), .Q(addr_latch_q));  // open: clr
  D_Flip_Flop #(.trigger("falling")) DMwe_latch (.D(WE), .clk(clk), .Q(DMwe_latch_q));  // open: Qn, preset, reset
  Register #(.width(16), .trigger("falling")) data_to_be_written (
    .D(data_in), .en(WE), .clk(clk), .Q(data_in_latched));  // open: clr
  Multiplexer #(.width(16), .enable("false")) multiplexer_1 (
    .in0(address), .in1(addr_latch_q), .out(address_latched), .sel(DMwe_latch_q));
  and and_1 (WE_latched, clk, DMwe_latch_q);
  not not_1 (OE_latched, WE_latched);
endmodule

module control (
  input  [3:0] opcode,
  output BR,
  output JP,
  output Rdst,
  output DMwe,
  output [1:0] ALUop,
  output ALUinB,
  output Rwd,
  output Rwe,
  output RwSSL,
  output RwSRL,
  output BLT,
  output JR,
  output JAL,
  output inputTrue,
  output outputTrue
);

  wire decoder_1_out0, decoder_1_out1, decoder_1_out2, decoder_1_out3, decoder_1_out4;

  Decoder #(.select(4), .enable("false")) decoder_1 (
    .out0(decoder_1_out0), .out1(decoder_1_out1), .out2(decoder_1_out2), .out3(decoder_1_out3),
    .out4(decoder_1_out4), .out5(RwSSL), .out6(RwSRL), .out7(Rwd), .out8(DMwe), .out9(BR), .out10(BLT),
    .out11(JP), .out12(JR), .out13(JAL), .out14(inputTrue), .out15(outputTrue), .sel(opcode));
  or or_1 (Rwe, JAL, decoder_1_out1, RwSSL, decoder_1_out4, decoder_1_out0, decoder_1_out2, inputTrue, decoder_1_out3, Rwd, RwSRL);
  or or_2 (Rdst, RwSSL, decoder_1_out0, decoder_1_out1, inputTrue, decoder_1_out3, decoder_1_out4, RwSRL);
  or or_3 (ALUinB, decoder_1_out2, Rwd, DMwe);
  or or_4 (ALUop[1], decoder_1_out4, decoder_1_out3);
  or or_5 (ALUop[0], BR, decoder_1_out3, decoder_1_out1, BLT);

  // Notes on the sheet:
  //   add
  //   sub
  //   addi
  //   not
  //   xor
  //   sll
  //   srl
  //   lw
  //   sw
  //   beqz
  //   blt
  //   j
  //   jr
  //   jal
  //   input
  //   output
endmodule

module leftShifter (
  input  [15:0] shiftInput,
  input  [2:0] shiftAmount,
  output [15:0] sllOutput
);

  Multiplexer #(.select(3), .width(16), .enable("false")) multiplexer_1 (
    .in0(shiftInput), .in1({shiftInput[14:0], 1'b0}), .in2({shiftInput[13:0], 2'b00}),
    .in3({shiftInput[12:0], 3'b000}), .in4({shiftInput[11:0], 4'b0000}), .in5({shiftInput[10:0], {5{1'b0}}}),
    .in6({shiftInput[9:0], {6{1'b0}}}), .in7({shiftInput[8:0], {7{1'b0}}}), .out(sllOutput), .sel(shiftAmount));

  // Other names for the same wires on the sheet: fiveShift[15:5] = shiftInput[10:0];
  //   fourShift[15:4] = shiftInput[11:0]; oneShift[15:1] = shiftInput[14:0]; threeShift[15:3] = shiftInput[12:0];
  //   twoShift[15:2] = shiftInput[13:0]; sevenShift[15:7] = shiftInput[8:0]; sixShift[15:6] = shiftInput[9:0]
endmodule

module rightShifter (
  input  [15:0] shiftInput,
  input  [2:0] shiftAmount,
  output [15:0] srlOutput
);

  Multiplexer #(.select(3), .width(16), .enable("false")) multiplexer_1 (
    .in0(shiftInput), .in1({1'b0, shiftInput[15:1]}), .in2({2'b00, shiftInput[15:2]}),
    .in3({3'b000, shiftInput[15:3]}), .in4({4'b0000, shiftInput[15:4]}), .in5({{5{1'b0}}, shiftInput[15:5]}),
    .in6({{6{1'b0}}, shiftInput[15:6]}), .in7({{7{1'b0}}, shiftInput[15:7]}), .out(srlOutput),
    .sel(shiftAmount));

  // Other names for the same wires on the sheet: fiveShift[10:0] = shiftInput[15:5];
  //   fourShift[11:0] = shiftInput[15:4]; oneShift[14:0] = shiftInput[15:1]; threeShift[12:0] = shiftInput[15:3];
  //   twoShift[13:0] = shiftInput[15:2]; sevenShift[8:0] = shiftInput[15:7]; sixShift[9:0] = shiftInput[15:6]
endmodule
